# Fritzing sketch Projeto (saved by Fritzing 0.9.4)
breadboards: 1

parts:
  LED17 = LED - 5mm [color="Green (570nm)" package="5 mm [THT]"]
  Componente1 = Arduino Uno (Rev3)
  R1 = Resistor [tolerance=±5% resistance=220 package=THT]
  R2 = Resistor [tolerance=±5% resistance=220 package=THT]
  R3 = Resistor [tolerance=±5% resistance=220 package=THT]
  R4 = Resistor [tolerance=±5% resistance=220 package=THT]
  R5 = Resistor [tolerance=±5% resistance=220 package=THT]
  R6 = Resistor [tolerance=±5% resistance=220 package=THT]
  R7 = Resistor [tolerance=±5% resistance=220 package=THT]
  R8 = Resistor [tolerance=±5% resistance=220 package=THT]
  R9 = Resistor [tolerance=±5% resistance=220 package=THT]
  R10 = Resistor [tolerance=±5% resistance=220 package=THT]
  R11 = Resistor [tolerance=±5% resistance=220 package=THT]
  R12 = Resistor [tolerance=±5% resistance=220 package=THT]
  R13 = Resistor [tolerance=±5% resistance=220 package=THT]
  R14 = Resistor [tolerance=±5% resistance=220 package=THT]
  R15 = Resistor [tolerance=±5% resistance=220 package=THT]
  R16 = Resistor [tolerance=±5% resistance=220 package=THT]
  Q1 = TRANSISTOR_NPN [package=to-92-ammo]
  Q2 = TRANSISTOR_NPN [package=to-92-ammo]
  Q3 = TRANSISTOR_NPN [package=to-92-ammo]
  Q4 = TRANSISTOR_NPN [package=to-92-ammo]
  R17 = Resistor [tolerance=±5% resistance=10k package=THT]
  R19 = Resistor [tolerance=±5% resistance=10k package=THT]
  R20 = Resistor [tolerance=±5% resistance=10k package=THT]
  R21 = Resistor [tolerance=±5% resistance=10k package=THT]
  R22 = Resistor [tolerance=±5% resistance=220 package="2010 [SMD]"]
  R23 = Resistor [tolerance=±5% resistance=220 package="2010 [SMD]"]
  R24 = Resistor [tolerance=±5% resistance=220 package="2010 [SMD]"]
  R25 = Resistor [tolerance=±5% resistance=220 package="2010 [SMD]"]
  R26 = Resistor [tolerance=±5% resistance=220 package="2010 [SMD]"]
  R27 = Resistor [tolerance=±5% resistance=220 package="2010 [SMD]"]
  R28 = Resistor [tolerance=±5% resistance=220 package="2010 [SMD]"]
  R29 = Resistor [tolerance=±5% resistance=220 package="2010 [SMD]"]
  R30 = Resistor [tolerance=±5% resistance=220 package="2010 [SMD]"]
  R31 = Resistor [tolerance=±5% resistance=220 package="2010 [SMD]"]
  R32 = Resistor [tolerance=±5% resistance=220 package="2010 [SMD]"]
  R33 = Resistor [tolerance=±5% resistance=220 package="2010 [SMD]"]
  R34 = Resistor [tolerance=±5% resistance=220 package="2010 [SMD]"]
  R35 = Resistor [tolerance=±5% resistance=220 package="2010 [SMD]"]
  R36 = Resistor [tolerance=±5% resistance=220 package="2010 [SMD]"]
  R37 = Resistor [tolerance=±5% resistance=220 package="2010 [SMD]"]
  R38 = Resistor [tolerance=±5% resistance=10k package=THT]
  Q5 = NPN-Transistor [package="TO92 [THT]"]
  Q6 = NPN-Transistor [package="TO92 [THT]"]
  Q7 = NPN-Transistor [package="TO92 [THT]"]
  Q8 = NPN-Transistor [package="TO92 [THT]"]
  R39 = Resistor [tolerance=±5% resistance=10k package=THT]
  R40 = Resistor [tolerance=±5% resistance=10k package=THT]
  R41 = Resistor [tolerance=±5% resistance=10k package=THT]
  LED68 = LED - 5mm [color="Green (570nm)" package="5 mm [THT]"]
  LED69 = LED - 5mm [color="Green (570nm)" package="5 mm [THT]"]
  LED70 = LED - 5mm [color="Green (570nm)" package="5 mm [THT]"]
  LED71 = LED - 5mm [color="Green (570nm)" package="5 mm [THT]"]
  LED72 = LED - 5mm [color="Green (570nm)" package="5 mm [THT]"]
  LED73 = LED - 5mm [color="Green (570nm)" package="5 mm [THT]"]
  LED74 = LED - 5mm [color="Green (570nm)" package="5 mm [THT]"]
  LED75 = LED - 5mm [color="Green (570nm)" package="5 mm [THT]"]
  LED76 = LED - 5mm [color="Green (570nm)" package="5 mm [THT]"]
  LED77 = LED - 5mm [color="Green (570nm)" package="5 mm [THT]"]
  LED78 = LED - 5mm [color="Green (570nm)" package="5 mm [THT]"]
  LED116 = LED - 5mm [color="Green (570nm)" package="5 mm [THT]"]
  LED117 = LED - 5mm [color="Green (570nm)" package="5 mm [THT]"]
  LED152 = LED - 5mm [color="Green (570nm)" package="5 mm [THT]"]
  LED118 = LED - 5mm [color="Green (570nm)" package="5 mm [THT]"]
  LED153 = LED - 5mm [color="Blue (505nm)" package="5 mm [THT]"]
  LED154 = LED - 5mm [color="Blue (505nm)" package="5 mm [THT]"]
  LED155 = LED - 5mm [color="Blue (505nm)" package="5 mm [THT]"]
  LED156 = LED - 5mm [color="Blue (505nm)" package="5 mm [THT]"]
  LED157 = LED - 5mm [color="Blue (505nm)" package="5 mm [THT]"]
  LED158 = LED - 5mm [color="Blue (505nm)" package="5 mm [THT]"]  # not connected
  LED159 = LED - 5mm [color="Blue (505nm)" package="5 mm [THT]"]  # not connected
  LED160 = LED - 5mm [color="Blue (505nm)" package="5 mm [THT]"]
  LED161 = LED - 5mm [color="Blue (505nm)" package="5 mm [THT]"]
  LED162 = LED - 5mm [color="Blue (505nm)" package="5 mm [THT]"]
  LED163 = LED - 5mm [color="Blue (505nm)" package="5 mm [THT]"]  # not connected
  LED164 = LED - 5mm [color="Blue (505nm)" package="5 mm [THT]"]  # not connected
  LED165 = LED - 5mm [color="Blue (505nm)" package="5 mm [THT]"]  # not connected
  LED166 = LED - 5mm [color="Blue (505nm)" package="5 mm [THT]"]  # not connected
  LED167 = LED - 5mm [color="Blue (505nm)" package="5 mm [THT]"]  # not connected
  LED168 = LED - 5mm [color="Blue (505nm)" package="5 mm [THT]"]  # not connected
  LED169 = LED - 5mm [color="Red (633nm)" package="5 mm [THT]"]
  LED170 = LED - 5mm [color="Red (633nm)" package="5 mm [THT]"]
  LED171 = LED - 5mm [color="Red (633nm)" package="5 mm [THT]"]
  LED172 = LED - 5mm [color="Red (633nm)" package="5 mm [THT]"]
  LED173 = LED - 5mm [color="Red (633nm)" package="5 mm [THT]"]
  LED174 = LED - 5mm [color="Red (633nm)" package="5 mm [THT]"]  # not connected
  LED175 = LED - 5mm [color="Red (633nm)" package="5 mm [THT]"]  # not connected
  LED176 = LED - 5mm [color="Red (633nm)" package="5 mm [THT]"]
  LED177 = LED - 5mm [color="Red (633nm)" package="5 mm [THT]"]
  LED178 = LED - 5mm [color="Red (633nm)" package="5 mm [THT]"]
  LED179 = LED - 5mm [color="Red (633nm)" package="5 mm [THT]"]  # not connected
  LED180 = LED - 5mm [color="Red (633nm)" package="5 mm [THT]"]  # not connected
  LED181 = LED - 5mm [color="Red (633nm)" package="5 mm [THT]"]  # not connected
  LED182 = LED - 5mm [color="Red (633nm)" package="5 mm [THT]"]  # not connected
  LED183 = LED - 5mm [color="Red (633nm)" package="5 mm [THT]"]  # not connected
  LED184 = LED - 5mm [color="Red (633nm)" package="5 mm [THT]"]  # not connected
  LED185 = LED - 5mm [color="Yellow (595nm)" package="5 mm [THT]"]
  LED186 = LED - 5mm [color="Yellow (595nm)" package="5 mm [THT]"]
  LED187 = LED - 5mm [color="Yellow (595nm)" package="5 mm [THT]"]
  LED188 = LED - 5mm [color="Yellow (595nm)" package="5 mm [THT]"]
  LED189 = LED - 5mm [color="Yellow (595nm)" package="5 mm [THT]"]
  LED190 = LED - 5mm [color="Yellow (595nm)" package="5 mm [THT]"]  # not connected
  LED191 = LED - 5mm [color="Yellow (595nm)" package="5 mm [THT]"]  # not connected
  LED192 = LED - 5mm [color="Yellow (595nm)" package="5 mm [THT]"]
  LED193 = LED - 5mm [color="Yellow (595nm)" package="5 mm [THT]"]
  LED194 = LED - 5mm [color="Yellow (595nm)" package="5 mm [THT]"]
  LED195 = LED - 5mm [color="Yellow (595nm)" package="5 mm [THT]"]  # not connected
  LED196 = LED - 5mm [color="Yellow (595nm)" package="5 mm [THT]"]  # not connected
  LED197 = LED - 5mm [color="Yellow (595nm)" package="5 mm [THT]"]  # not connected
  LED198 = LED - 5mm [color="Yellow (595nm)" package="5 mm [THT]"]  # not connected
  LED199 = LED - 5mm [color="Yellow (595nm)" package="5 mm [THT]"]  # not connected
  LED200 = LED - 5mm [color="Yellow (595nm)" package="5 mm [THT]"]  # not connected

nets:
  N1: LED17.cathode, LED68.cathode, LED69.cathode, LED70.cathode, LED71.cathode, LED74.cathode, LED75.cathode, LED76.cathode
  N2: LED17.anode, R15.Pin_1, R32.Pin_1
  N3: Componente1.A2, R19.Pin_0, R39.Pin_0
  N4: Componente1.A3, R20.Pin_0, R40.Pin_0
  N5: Componente1.A4/SDA, R21.Pin_0, R41.Pin_0
  N6: Componente1.A5/SCL, R17.Pin_0, R38.Pin_0
  N7: Componente1.D8, R8.Pin_0, R27.Pin_0
  N8: Componente1.D9_PWM, R7.Pin_0, R26.Pin_0
  N9: Componente1.D10_PWM/SS, R6.Pin_0, R25.Pin_0
  N10: Componente1.D11_PWM/MOSI, R5.Pin_0, R24.Pin_0
  N11: Componente1.D12/MISO, R1.Pin_0, R22.Pin_0
  N12: Componente1.D13/SCK, R9.Pin_0, R23.Pin_0
  N13: Componente1.GND, Q1.E, Q2.E, Q3.E, Q4.E, Q5.E, Q6.E, Q7.E, Q8.E
  N14: Componente1.D0/RX, R13.Pin_0, R35.Pin_0
  N15: Componente1.D1/TX, R12.Pin_0, R34.Pin_0
  N16: Componente1.D2, R11.Pin_0, R33.Pin_0
  N17: Componente1.D3_PWM, R10.Pin_0, R31.Pin_0
  N18: Componente1.D4, R16.Pin_0, R37.Pin_0
  N19: Componente1.D5_PWM, R2.Pin_0, R30.Pin_0
  N20: Componente1.D6_PWM, R3.Pin_0, R29.Pin_0
  N21: Componente1.D7, R4.Pin_0, R28.Pin_0
  N22: R1.Pin_1, R22.Pin_1, LED69.anode
  N23: R2.Pin_1, R30.Pin_1, LED78.anode
  N24: R3.Pin_1, R29.Pin_1, LED72.anode
  N25: R4.Pin_1, R28.Pin_1, LED118.anode
  N26: R5.Pin_1, R24.Pin_1, LED70.anode
  N27: R6.Pin_1, R25.Pin_1, LED71.anode
  N28: R7.Pin_1, R26.Pin_1, LED77.anode
  N29: R8.Pin_1, R27.Pin_1, LED152.anode
  N30: R9.Pin_1, R23.Pin_1, LED68.anode
  N31: R10.Pin_1, R31.Pin_1, LED116.anode
  N32: R11.Pin_1, R33.Pin_1, LED73.anode
  N33: R12.Pin_1, R34.Pin_1, LED76.anode
  N34: R13.Pin_1, R35.Pin_1, LED75.anode
  N35: R14.Pin_0, R36.Pin_0
  N36: R14.Pin_1, R36.Pin_1, LED74.anode
  N37: R15.Pin_0, R32.Pin_0
  N38: R16.Pin_1, R37.Pin_1, LED117.anode
  N39: Q1.B, R17.Pin_1, R38.Pin_1, Q5.B
  N40: Q1.C, Q5.C
  N41: Q2.B, R21.Pin_1, Q8.B, R41.Pin_1
  N42: Q2.C, Q8.C
  N43: Q3.B, R20.Pin_1, Q6.B, R40.Pin_1
  N44: Q3.C, Q6.C
  N45: Q4.B, R19.Pin_1, Q7.B, R39.Pin_1
  N46: Q4.C, Q7.C
  N47: LED153.cathode, LED154.cathode, LED155.cathode, LED156.cathode, LED157.cathode, LED160.cathode, LED161.cathode, LED162.cathode
  N48: LED169.cathode, LED170.cathode, LED171.cathode, LED172.cathode, LED173.cathode, LED176.cathode, LED177.cathode, LED178.cathode
  N49: LED185.cathode, LED186.cathode, LED187.cathode, LED188.cathode, LED189.cathode, LED192.cathode, LED193.cathode, LED194.cathode

// code stored in the sketch: Codigo.ino
int Columnas[] = {0, 1, 2, 3, 4, 5, 6, 7, 8, 9, 10, 11, 12, 13, 14, 15};   
int Filas[] = {16, 17, 18, 19};

int RandFila;     //Variable para fila aleatoria
int RandColumna;  //Variable para columna aleatoria
   
void setup()
{
int contador;
   
for (int contador = 0; contador < 17; contador++){
  pinMode(Columnas[contador], OUTPUT); }
   
for (int contador = 0; contador < 5; contador++){
  pinMode(Filas[contador], OUTPUT); }
}
   
void loop()
{
RandLed();
}
   
void RandLed()
{
RandFila = random(0,4);
RandColumna = random(0,16);
   
digitalWrite(Filas[RandFila], HIGH);
digitalWrite(Columnas[RandColumna], HIGH);
   
delay(75);
   
digitalWrite(Filas[RandFila], LOW);
digitalWrite(Columnas[RandColumna], LOW);
   
delay(50);
}
